# Fritzing sketch knightr0s_gambit_fritzing_diagram (saved by Fritzing 0.9.9b)
breadboards: 2

parts:
  Part1 = EasyDriver_v44
  U2 = V_REG_LD1117VXX [package=78xxl]
  Mod1 = Raspberry Pi 4B
  M1 = Stepper Motor - Bipolar
  R1 = Resistor [tolerance=±5% power=0.25 resistance=220 package=THT]
  D2 = Schottky Diode [part_number=1N5817 package="Melf DO-213 AB [SMD]"]
  M2 = Stepper Motor - Bipolar
  Part2 = EasyDriver_v44
  Q2 = MOSFET-NCHANNEL [package=to220v]
  L2 = Inductor [package="0805 [SMD]"]
  J1 = Power Jack [package=power_jack_pth_lock]
  S1 = Round Pushbutton
  R2 = Resistor [tolerance=±5% power=0.25 resistance=220 package=THT]
  U3 = LuaNode32 / ESP32 [part_number=ESP32S-PIN30]
  S8 = Limit Switch
  S9 = Limit Switch
  R7 = Resistor [tolerance=±5% power=0.25 resistance=220 package=THT]
  R8 = Resistor [tolerance=±5% power=0.25 resistance=220 package=THT]
  R9 = Resistor [tolerance=±5% power=0.25 resistance=220 package=THT]
  R10 = Resistor [tolerance=±5% power=0.25 resistance=220 package=THT]
  S10 = Limit Switch
  S11 = Limit Switch
  R11 = Resistor [tolerance=±5% power=0.25 resistance=220 package=THT]

nets:
  GND: Part1.GND, U2.GND, Part2.GND, Q2.S, J1.GND, R2.Pin_0, U3.GND, R7.Pin_1, R8.Pin_1, R9.Pin_1, R10.Pin_1
  N1: Part1.V+, U2.IN, R1.Pin_0, D2.cathode, Part2.V+, J1.PWR
  N2: Part1.STEP, U3.D14
  N3: Part1.DIR, U3.D27
  N4: Part1.OUT2A, M1.A
  N5: Part1.OUT2B, M1.C
  N6: Part1.OUT1A, M1.B
  N7: Part1.OUT1B, M1.D
  N8: Part1.MS1, U3.D13
  N9: Part1.SLEEP, U3.D15
  N10: Part1.ENABLE, Part2.ENABLE, U3.D4
  N11: Part1.MS2, U3.D12
  N12: Part1.RESET, Part2.RESET, U3.D2
  N13: U2.OUT, U3.EN, U3.Vin, S8.leg0, S9.leg0, S10.leg0, S11.leg0
  N14: Mod1.GPIO14, U3.RX2
  N15: Mod1.GPIO15, U3.TX2
  N16: R1.Pin_1, L2.pin_0
  N17: D2.anode, Q2.D, L2.pin_1
  N18: M2.A, Part2.OUT2A
  N19: M2.C, Part2.OUT2B
  N20: M2.B, Part2.OUT1A
  N21: M2.D, Part2.OUT1B
  N22: Part2.STEP, U3.D33
  N23: Part2.DIR, U3.D32
  N24: Part2.MS1, U3.D26
  N25: Part2.MS2, U3.D25
  N26: Q2.G, R11.Pin_0
  N27: S1.leg1, R2.Pin_1, U3.D21
  N28: U3.VP, R8.Pin_0, S11.leg1
  N29: U3.VN, S8.leg1, R10.Pin_0
  N30: U3.D34, R7.Pin_0, S10.leg1
  N31: U3.D35, S9.leg1, R9.Pin_0
  N32: U3.D23, R11.Pin_1

notes:
  Electromagnet
  12V
  Raspberry Pi
  Motors
  ESP32
  EasyDriver Boards
  Chess Timer
  End Stop

custom parts:
  LuaNode32 / ESP32: New Image for LuaNode32 DOIT ESP32 DEVKIT V1. Base parts from LuaNode32 / ESP32 ESP32 based LuaNode32 by G.Noorlander DOIT Esp32 DevKit v1 (30 pins long, 11 pins width) by Werner Rothschopf (modified by vanepp Dec 2018)
  Limit Switch: A generic limit switch
